# Fritzing sketch Drone-Schematic (saved by Fritzing 0.9.3b)
breadboards: 1

parts:
  Q1 = NPN-Transistor [package="TO92 [THT]"]
  R1 = Resistor [tolerance=±5% resistance=6.5 package=THT]
  R2 = Resistor [tolerance=±5% resistance=47 package=THT]
  Bauteil1 = Arduino Pro Mini v13
  U1 = LIPO-110mAh [package=lipo-110]
  Q2 = NPN-Transistor [package="TO92 [THT]"]
  R3 = Resistor [tolerance=±5% resistance=6.5 package=THT]
  R4 = Resistor [tolerance=±5% resistance=47 package=THT]
  Q3 = NPN-Transistor [package="TO92 [THT]"]
  R5 = Resistor [tolerance=±5% resistance=6.5 package=THT]
  R6 = Resistor [tolerance=±5% resistance=47 package=THT]
  Q4 = NPN-Transistor [package="TO92 [THT]"]
  R7 = Resistor [tolerance=±5% resistance=6.5 package=THT]
  R8 = Resistor [tolerance=±5% resistance=47 package=THT]
  C1 = Electrolytic Capacitor [capacitance=10µF package="100 mil [THT, electrolytic]"]
  C2 = Electrolytic Capacitor [capacitance=10µF package="100 mil [THT, electrolytic]"]
  C3 = Electrolytic Capacitor [capacitance=10µF package="100 mil [THT, electrolytic]"]
  C4 = Electrolytic Capacitor [capacitance=10µF package="100 mil [THT, electrolytic]"]
  C5 = Electrolytic Capacitor [capacitance=220µF package="100 mil [THT, electrolytic]"]
  3-Axis_Accelerometer1 = 3-Axis Accelerometer Breakout - MMA8452Q
  Bauteil2 = Adafruit RFM9x LoRa Radio [part_number="Adafruit #3072 and #3073"]
  ANT1 = Antenna
  LED1 = LED - 3mm [color="Red (633nm)" package="3 mm [THT]"]
  R9 = Resistor [tolerance=±5% resistance=220 package=THT]
  U2 = Voltage Regulator -- 3.3 V -- LM1117

nets:
  N1: Q1.E, R1.Pin_1, Bauteil1.A1, C1.+
  N2: Q1.B, R2.Pin_1
  N3: Q1.C, U1.+, Q2.C, Q3.C, Q4.C, C5.+, U2.IN
  N4: R1.Pin_0, U1.-, R3.Pin_0, R5.Pin_0, R7.Pin_0, C1.-, C2.-, C3.-, C4.-, C5.-
  N5: R2.Pin_0, Bauteil1.D6_PWM
  N6: Bauteil1.VCC, U2.OUT
  GND: Bauteil1.GND, 3-Axis_Accelerometer1.GND, Bauteil2.GND, LED1.cathode, U2.GND
  N7: Bauteil1.A4, 3-Axis_Accelerometer1.SDA
  N8: Bauteil1.A5, 3-Axis_Accelerometer1.SCL
  N9: Bauteil1.A3, Q4.E, R7.Pin_1, C4.+
  N10: Bauteil1.A2, Q3.E, R5.Pin_1, C3.+
  N11: Bauteil1.A0, Q2.E, R3.Pin_1, C2.+
  N12: Bauteil1.D13/SCK, Bauteil2.SCK
  N13: Bauteil1.D12/MISO, Bauteil2.MISO
  N14: Bauteil1.D11_PWM/MOSI, Bauteil2.MOSI
  N15: Bauteil1.D10_PWM/SS, Bauteil2.CS
  N16: Bauteil1.D9_PWM, R6.Pin_0
  N17: Bauteil1.D8, Bauteil2.DIO1
  N18: Bauteil1.D7, Bauteil2.DIO0
  N19: Bauteil1.D5_PWM, R8.Pin_0
  N20: Bauteil1.D4, Bauteil2.RST
  N21: Bauteil1.D3_PWM, R4.Pin_0
  N22: Bauteil1.D2, R9.Pin_0
  N23: Q2.B, R4.Pin_1
  N24: Q3.B, R6.Pin_1
  N25: Q4.B, R8.Pin_1
  3.3V: 3-Axis_Accelerometer1.3.3V, Bauteil2.VIN
  N26: Bauteil2.ANTENNA, ANT1.antenna_lead
  N27: LED1.anode, R9.Pin_1

custom parts:
  Adafruit RFM9x LoRa Radio: Sending data over long distances is like magic, and now you can be a magician with this range of powerful and easy-to-use radio modules. Sure, sometimes you want to talk to a computer (a good time to use WiFi) or perhaps communicate with a Phone (choose Bluetooth Low Energy!) but what if you want to send data very far? Most WiFi, Bluetooth, Zigbee and other wireless chipsets use 2.4GHz, which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
  Voltage Regulator -- 3.3 V -- LM1117: LM1117-3.3 Voltage regulator, 3.3 V output. Note that the pinout order is not the same as LM7805 or LM7833.
